# Fritzing sketch SleepingSensors (saved by Fritzing 0.8.7b)
breadboards: 1

parts:
  Arduino = Arduino Mega 2560 (Rev3)
  R1 = Photocell (LDR) [package=THT]
  R2 = Temperature Sensor (Thermistor) [thermistor_type=NTC package=THT]
  S1 = Pushbutton [package="[THT]"]
  C1 = Ceramic Capacitor [capacitance=100nF package="100 mil [THT, multilayer]"]
  R3 = Resistor [tolerance=±5% resistance=10k package=THT]
  R4 = Resistor [tolerance=±5% resistance=10k package=THT]
  LCD1 = LCD screen
  R5 = Rotary Potentiometer (Small) [maximum_resistance=100kΩ package=THT]
  R6 = Resistor [tolerance=±5% resistance=220 package=THT]
  Q1 = PNP-Transistor [part_number=BC337-40 package="TO92 [THT]"]
  R7 = Resistor [tolerance=±5% resistance=10k package=THT]

nets:
  N1: Arduino.A0, R1.pin_1, R3.Pin_0
  N2: Arduino.A1, R2.pin_1, R4.Pin_0
  N3: Arduino.D21/SCL, Arduino.SCL, R7.Pin_0
  N4: Arduino.D20/SDA, Arduino.SDA, S1.Pin_1, S1.Pin_2, C1.1
  5V: Arduino.5V, R1.pin_0, R2.pin_0, LCD1.VDD, R5.leg1, R6.Pin_0
  GND: Arduino.GND, S1.Pin_3, S1.Pin_4, C1.0, R3.Pin_1, R4.Pin_1, LCD1.VSS, LCD1.R/W, Q1.C
  N5: Arduino.D22, LCD1.DB4
  N6: Arduino.D23, LCD1.DB5
  N7: Arduino.D24, LCD1.DB6
  N8: Arduino.D25, LCD1.DB7
  N9: Arduino.D26, LCD1.RS
  N10: Arduino.D27, LCD1.E
  N11: LCD1.V0, R5.wiper
  N12: LCD1.LED+, R6.Pin_1
  N13: LCD1.LED-, R5.leg2, Q1.E
  N14: Q1.B, R7.Pin_1
